// Logisim project Processador.circ as structural Verilog: 8 circuits, main circuit main
module main (
  input  R___W,
  input  [10:0] Input
);

  wire clock_1_out;
  wire [2:0] contador_1_out_2;
  wire [7:0] acumulador_1_output, ula_1_s;
  wire [10:0] \memória_1_s ;

  Contador contador_1 (.out_2(contador_1_out_2), .in_1(clock_1_out));
  Clock clock_1 (.out(clock_1_out));
  \Memória  \memória_1  (.Input(Input), .R___W(R___W), .S(\memória_1_s ), .Address(contador_1_out_2));
  // Probe on acumulador_1_output
  ULA ula_1 (.A(acumulador_1_output), .B(\memória_1_s [7:0]), .S(ula_1_s), .Seletor(\memória_1_s [10:8]));
  Acumulador acumulador_1 (.Input(ula_1_s), .R___W(clock_1_out), .Output(acumulador_1_output));

  // Notes on the sheet:
  //   Artur Pigari Prata - 2101297
  //   000 AND
  //   001 OR
  //   010 XOR
  //   011 SOMA
  //   Comandos do Seletor
  //   100 SUBTRAÇÃO
  //   110 DIVISÃO
  //   111 RESTO
  //   101 MULTIPLICAÇÃO
endmodule

module ULA (
  input  [7:0] A,
  input  [7:0] B,
  input  [2:0] Seletor,
  output [7:0] S
);

  wire and_1_out, and_2_out, and_3_out, and_4_out, and_5_out, and_6_out, and_7_out, and_8_out;
  wire [7:0] and_9_out, and_10_out, and_11_out, and_12_out, and_13_out, and_14_out, and_15_out, and_16_out,
       divider_1_out, divider_1_rem, multiplier_1_out, or_1_out, or_2_out, output8_1_out_2, output8_2_out_2,
       output8_3_out_2, output8_4_out_2, output8_5_out_2, output8_6_out_2, output8_7_out_2, output8_8_out_2,
       somador_subtrator_1_s, xor_1_out;

  and and_1 (and_1_out, ~Seletor[2], ~Seletor[1], ~Seletor[0]);  // AND_Gate
  output8 output8_1 (.in_1(and_1_out), .out_2(output8_1_out_2));
  and and_2 (and_2_out, ~Seletor[2], ~Seletor[1], Seletor[0]);  // AND_Gate
  output8 output8_2 (.in_1(and_2_out), .out_2(output8_2_out_2));
  and and_3 (and_3_out, ~Seletor[2], Seletor[1], ~Seletor[0]);  // AND_Gate
  output8 output8_3 (.in_1(and_3_out), .out_2(output8_3_out_2));
  output8 output8_4 (.in_1(and_4_out), .out_2(output8_4_out_2));
  and and_4 (and_4_out, ~Seletor[2], Seletor[1], Seletor[0]);  // AND_Gate
  and and_5 (and_5_out, Seletor[2], ~Seletor[1], ~Seletor[0]);  // AND_Gate
  output8 output8_5 (.in_1(and_6_out), .out_2(output8_5_out_2));
  and and_6 (and_6_out, Seletor[2], ~Seletor[1], Seletor[0]);  // AND_Gate
  and and_7 (and_7_out, Seletor[2], Seletor[1], ~Seletor[0]);  // AND_Gate
  output8 output8_6 (.in_1(and_7_out), .out_2(output8_6_out_2));
  output8 output8_7 (.in_1(and_8_out), .out_2(output8_7_out_2));
  and and_8 (and_8_out, Seletor[2], Seletor[1], Seletor[0]);
  // Probe on A
  // Probe on B
  assign and_9_out = A & B;  // AND_Gate and_9, 8 bits wide
  assign or_1_out = A | B;  // OR_Gate or_1, 8 bits wide
  somador_subtrator somador_subtrator_1 (.A(A), .B(B), .in_3(and_5_out), .S(somador_subtrator_1_s));
  assign or_2_out = output8_4_out_2 | output8_8_out_2;  // OR_Gate or_2, 8 bits wide
  output8 output8_8 (.in_1(and_5_out), .out_2(output8_8_out_2));
  assign and_10_out = and_9_out & output8_1_out_2;  // AND_Gate and_10, 8 bits wide
  assign and_11_out = or_1_out & output8_2_out_2;  // AND_Gate and_11, 8 bits wide
  assign xor_1_out = A ^ B;  // XOR_Gate xor_1, 8 bits wide
  assign and_12_out = xor_1_out & output8_3_out_2;  // AND_Gate and_12, 8 bits wide
  assign and_13_out = somador_subtrator_1_s & or_2_out;  // AND_Gate and_13, 8 bits wide
  Multiplier multiplier_1 (.a(A), .b(B), .out(multiplier_1_out));  // open: cin, cout
  assign and_14_out = multiplier_1_out & output8_5_out_2;  // AND_Gate and_14, 8 bits wide
  Divider divider_1 (.a(A), .b(B), .out(divider_1_out), .rem(divider_1_rem));  // open: upper
  assign and_15_out = divider_1_out & output8_6_out_2;  // AND_Gate and_15, 8 bits wide
  assign and_16_out = divider_1_rem & output8_7_out_2;  // AND_Gate and_16, 8 bits wide
  // Probe on S
  assign S = and_10_out | and_11_out | and_12_out | and_13_out | and_14_out | and_15_out | and_16_out;  // OR_Gate or_3, 8 bits wide

  // Notes on the sheet:
  //   Artur Pigari Prata - 2101297
  //   Comandos do Seletor
  //   000 AND
  //   001 OR
  //   010 XOR
  //   011 SOMA
  //   100 SUBTRAÇÃO
  //   101 MULTIPLICAÇÃO
  //   110 DIVISÃO
  //   111 RESTO
endmodule

module \Memória  (
  input  [10:0] Input,
  input  [2:0] Address,
  input  R___W,
  output [10:0] S
);

  wire and_1_out, and_2_out, and_3_out, and_4_out, and_5_out, and_6_out, and_7_out, and_8_out, and_9_out,
       and_10_out, and_11_out, and_12_out, and_13_out, and_14_out, and_15_out, and_16_out, and_17_out,
       and_18_out, and_19_out, and_20_out, and_21_out, and_22_out, and_23_out, and_24_out, and_25_out,
       and_26_out, and_27_out, and_28_out, and_29_out, and_30_out, and_31_out, and_32_out, and_33_out,
       and_34_out, and_35_out, and_36_out, and_37_out, and_38_out, and_39_out, and_40_out, and_41_out,
       and_42_out, and_43_out, and_44_out, and_45_out, and_46_out, and_47_out, and_48_out, and_49_out,
       and_50_out, and_51_out, and_52_out, and_53_out, and_54_out, and_55_out, and_56_out, and_57_out,
       and_58_out, and_59_out, and_60_out, and_61_out, and_62_out, and_63_out, and_64_out, and_65_out,
       and_66_out, and_67_out, and_68_out, and_69_out, and_70_out, and_71_out, and_72_out, and_73_out,
       and_74_out, and_75_out, and_76_out, and_77_out, and_78_out, and_79_out, and_80_out, and_81_out,
       and_82_out, and_83_out, and_84_out, and_85_out, and_86_out, and_87_out, and_88_out, and_89_out,
       and_90_out, and_91_out, and_92_out, and_93_out, and_94_out, and_95_out, and_96_out, and_97_out,
       and_98_out, and_99_out, and_100_out, and_101_out, and_102_out, and_103_out, and_104_out, d_ff_1_q,
       d_ff_2_q, d_ff_3_q, d_ff_4_q, d_ff_5_q, d_ff_6_q, d_ff_7_q, d_ff_8_q, d_ff_9_q, d_ff_10_q, d_ff_11_q,
       d_ff_12_q, d_ff_13_q, d_ff_14_q, d_ff_15_q, d_ff_16_q, d_ff_17_q, d_ff_18_q, d_ff_19_q, d_ff_20_q,
       d_ff_21_q, d_ff_22_q, d_ff_23_q, d_ff_24_q, d_ff_25_q, d_ff_26_q, d_ff_27_q, d_ff_28_q, d_ff_29_q,
       d_ff_30_q, d_ff_31_q, d_ff_32_q, d_ff_33_q, d_ff_34_q, d_ff_35_q, d_ff_36_q, d_ff_37_q, d_ff_38_q,
       d_ff_39_q, d_ff_40_q, d_ff_41_q, d_ff_42_q, d_ff_43_q, d_ff_44_q, d_ff_45_q, d_ff_46_q, d_ff_47_q,
       d_ff_48_q, d_ff_49_q, d_ff_50_q, d_ff_51_q, d_ff_52_q, d_ff_53_q, d_ff_54_q, d_ff_55_q, d_ff_56_q,
       d_ff_57_q, d_ff_58_q, d_ff_59_q, d_ff_60_q, d_ff_61_q, d_ff_62_q, d_ff_63_q, d_ff_64_q, d_ff_65_q,
       d_ff_66_q, d_ff_67_q, d_ff_68_q, d_ff_69_q, d_ff_70_q, d_ff_71_q, d_ff_72_q, d_ff_73_q, d_ff_74_q,
       d_ff_75_q, d_ff_76_q, d_ff_77_q, d_ff_78_q, d_ff_79_q, d_ff_80_q, d_ff_81_q, d_ff_82_q, d_ff_83_q,
       d_ff_84_q, d_ff_85_q, d_ff_86_q, d_ff_87_q, d_ff_88_q;

  and and_1 (and_1_out, ~Address[2], ~Address[1], ~Address[0]);  // AND_Gate
  and and_2 (and_2_out, ~Address[2], ~Address[1], Address[0]);  // AND_Gate
  and and_3 (and_3_out, ~Address[2], Address[1], ~Address[0]);  // AND_Gate
  and and_4 (and_4_out, ~Address[2], Address[1], Address[0]);  // AND_Gate
  and and_5 (and_5_out, Address[2], ~Address[1], ~Address[0]);  // AND_Gate
  and and_6 (and_6_out, Address[2], ~Address[1], Address[0]);  // AND_Gate
  and and_7 (and_7_out, Address[2], Address[1], ~Address[0]);  // AND_Gate
  and and_8 (and_8_out, Address[2], Address[1], Address[0]);
  and and_9 (and_9_out, and_1_out, R___W);
  D_Flip_Flop d_ff_1 (.clk(and_9_out), .D(Input[10]), .Q(d_ff_1_q));  // open: Qn, preset, en, reset
  and and_10 (and_10_out, and_2_out, R___W);
  D_Flip_Flop d_ff_2 (.clk(and_10_out), .D(Input[10]), .Q(d_ff_2_q));  // open: Qn, preset, en, reset
  and and_11 (and_11_out, and_3_out, R___W);
  D_Flip_Flop d_ff_3 (.clk(and_11_out), .D(Input[10]), .Q(d_ff_3_q));  // open: Qn, preset, en, reset
  and and_12 (and_12_out, and_4_out, R___W);
  D_Flip_Flop d_ff_4 (.clk(and_12_out), .D(Input[10]), .Q(d_ff_4_q));  // open: Qn, preset, en, reset
  and and_13 (and_13_out, and_5_out, R___W);
  D_Flip_Flop d_ff_5 (.clk(and_13_out), .D(Input[10]), .Q(d_ff_5_q));  // open: Qn, preset, en, reset
  and and_14 (and_14_out, and_6_out, R___W);
  D_Flip_Flop d_ff_6 (.clk(and_14_out), .D(Input[10]), .Q(d_ff_6_q));  // open: Qn, preset, en, reset
  and and_15 (and_15_out, and_7_out, R___W);
  D_Flip_Flop d_ff_7 (.clk(and_15_out), .D(Input[10]), .Q(d_ff_7_q));  // open: Qn, preset, en, reset
  and and_16 (and_16_out, and_8_out, R___W);
  D_Flip_Flop d_ff_8 (.clk(and_16_out), .D(Input[10]), .Q(d_ff_8_q));  // open: Qn, preset, en, reset
  or or_1 (S[10], and_24_out, and_23_out, and_22_out, and_21_out, and_20_out, and_19_out, and_18_out, and_17_out);
  and and_17 (and_17_out, and_1_out, d_ff_1_q);
  and and_18 (and_18_out, and_2_out, d_ff_2_q);
  and and_19 (and_19_out, and_3_out, d_ff_3_q);
  and and_20 (and_20_out, and_4_out, d_ff_4_q);
  and and_21 (and_21_out, and_5_out, d_ff_5_q);
  and and_22 (and_22_out, and_6_out, d_ff_6_q);
  and and_23 (and_23_out, and_7_out, d_ff_7_q);
  and and_24 (and_24_out, and_8_out, d_ff_8_q);
  D_Flip_Flop d_ff_9 (.clk(and_9_out), .D(Input[9]), .Q(d_ff_9_q));  // open: Qn, preset, en, reset
  D_Flip_Flop d_ff_10 (.clk(and_10_out), .D(Input[9]), .Q(d_ff_10_q));  // open: Qn, preset, en, reset
  D_Flip_Flop d_ff_11 (.clk(and_11_out), .D(Input[9]), .Q(d_ff_11_q));  // open: Qn, preset, en, reset
  D_Flip_Flop d_ff_12 (.clk(and_12_out), .D(Input[9]), .Q(d_ff_12_q));  // open: Qn, preset, en, reset
  D_Flip_Flop d_ff_13 (.clk(and_13_out), .D(Input[9]), .Q(d_ff_13_q));  // open: Qn, preset, en, reset
  D_Flip_Flop d_ff_14 (.clk(and_14_out), .D(Input[9]), .Q(d_ff_14_q));  // open: Qn, preset, en, reset
  D_Flip_Flop d_ff_15 (.clk(and_15_out), .D(Input[9]), .Q(d_ff_15_q));  // open: Qn, preset, en, reset
  D_Flip_Flop d_ff_16 (.clk(and_16_out), .D(Input[9]), .Q(d_ff_16_q));  // open: Qn, preset, en, reset
  or or_2 (S[9], and_32_out, and_31_out, and_30_out, and_29_out, and_28_out, and_27_out, and_26_out, and_25_out);
  and and_25 (and_25_out, and_1_out, d_ff_9_q);
  and and_26 (and_26_out, and_2_out, d_ff_10_q);
  and and_27 (and_27_out, and_3_out, d_ff_11_q);
  and and_28 (and_28_out, and_4_out, d_ff_12_q);
  and and_29 (and_29_out, and_5_out, d_ff_13_q);
  and and_30 (and_30_out, and_6_out, d_ff_14_q);
  and and_31 (and_31_out, and_7_out, d_ff_15_q);
  and and_32 (and_32_out, and_8_out, d_ff_16_q);
  D_Flip_Flop d_ff_17 (.clk(and_9_out), .D(Input[8]), .Q(d_ff_17_q));  // open: Qn, preset, en, reset
  and and_33 (and_33_out, and_1_out, d_ff_17_q);
  D_Flip_Flop d_ff_18 (.clk(and_10_out), .D(Input[8]), .Q(d_ff_18_q));  // open: Qn, preset, en, reset
  and and_34 (and_34_out, and_2_out, d_ff_18_q);
  D_Flip_Flop d_ff_19 (.clk(and_11_out), .D(Input[8]), .Q(d_ff_19_q));  // open: Qn, preset, en, reset
  and and_35 (and_35_out, and_3_out, d_ff_19_q);
  D_Flip_Flop d_ff_20 (.clk(and_12_out), .D(Input[8]), .Q(d_ff_20_q));  // open: Qn, preset, en, reset
  and and_36 (and_36_out, and_4_out, d_ff_20_q);
  D_Flip_Flop d_ff_21 (.clk(and_13_out), .D(Input[8]), .Q(d_ff_21_q));  // open: Qn, preset, en, reset
  and and_37 (and_37_out, and_5_out, d_ff_21_q);
  D_Flip_Flop d_ff_22 (.clk(and_14_out), .D(Input[8]), .Q(d_ff_22_q));  // open: Qn, preset, en, reset
  and and_38 (and_38_out, and_6_out, d_ff_22_q);
  D_Flip_Flop d_ff_23 (.clk(and_15_out), .D(Input[8]), .Q(d_ff_23_q));  // open: Qn, preset, en, reset
  and and_39 (and_39_out, and_7_out, d_ff_23_q);
  D_Flip_Flop d_ff_24 (.clk(and_16_out), .D(Input[8]), .Q(d_ff_24_q));  // open: Qn, preset, en, reset
  and and_40 (and_40_out, and_8_out, d_ff_24_q);
  or or_3 (S[8], and_40_out, and_39_out, and_38_out, and_37_out, and_36_out, and_35_out, and_34_out, and_33_out);
  D_Flip_Flop d_ff_25 (.clk(and_9_out), .D(Input[7]), .Q(d_ff_25_q));  // open: Qn, preset, en, reset
  D_Flip_Flop d_ff_26 (.clk(and_10_out), .D(Input[7]), .Q(d_ff_26_q));  // open: Qn, preset, en, reset
  D_Flip_Flop d_ff_27 (.clk(and_11_out), .D(Input[7]), .Q(d_ff_27_q));  // open: Qn, preset, en, reset
  D_Flip_Flop d_ff_28 (.clk(and_12_out), .D(Input[7]), .Q(d_ff_28_q));  // open: Qn, preset, en, reset
  D_Flip_Flop d_ff_29 (.clk(and_13_out), .D(Input[7]), .Q(d_ff_29_q));  // open: Qn, preset, en, reset
  D_Flip_Flop d_ff_30 (.clk(and_14_out), .D(Input[7]), .Q(d_ff_30_q));  // open: Qn, preset, en, reset
  D_Flip_Flop d_ff_31 (.clk(and_15_out), .D(Input[7]), .Q(d_ff_31_q));  // open: Qn, preset, en, reset
  D_Flip_Flop d_ff_32 (.clk(and_16_out), .D(Input[7]), .Q(d_ff_32_q));  // open: Qn, preset, en, reset
  or or_4 (S[7], and_48_out, and_47_out, and_46_out, and_45_out, and_44_out, and_43_out, and_42_out, and_41_out);
  and and_41 (and_41_out, and_1_out, d_ff_25_q);
  and and_42 (and_42_out, and_2_out, d_ff_26_q);
  and and_43 (and_43_out, and_3_out, d_ff_27_q);
  and and_44 (and_44_out, and_4_out, d_ff_28_q);
  and and_45 (and_45_out, and_5_out, d_ff_29_q);
  and and_46 (and_46_out, and_6_out, d_ff_30_q);
  and and_47 (and_47_out, and_7_out, d_ff_31_q);
  and and_48 (and_48_out, and_8_out, d_ff_32_q);
  D_Flip_Flop d_ff_33 (.clk(and_9_out), .D(Input[6]), .Q(d_ff_33_q));  // open: Qn, preset, en, reset
  D_Flip_Flop d_ff_34 (.clk(and_10_out), .D(Input[6]), .Q(d_ff_34_q));  // open: Qn, preset, en, reset
  D_Flip_Flop d_ff_35 (.clk(and_11_out), .D(Input[6]), .Q(d_ff_35_q));  // open: Qn, preset, en, reset
  D_Flip_Flop d_ff_36 (.clk(and_12_out), .D(Input[6]), .Q(d_ff_36_q));  // open: Qn, preset, en, reset
  D_Flip_Flop d_ff_37 (.clk(and_13_out), .D(Input[6]), .Q(d_ff_37_q));  // open: Qn, preset, en, reset
  D_Flip_Flop d_ff_38 (.clk(and_14_out), .D(Input[6]), .Q(d_ff_38_q));  // open: Qn, preset, en, reset
  D_Flip_Flop d_ff_39 (.clk(and_15_out), .D(Input[6]), .Q(d_ff_39_q));  // open: Qn, preset, en, reset
  D_Flip_Flop d_ff_40 (.clk(and_16_out), .D(Input[6]), .Q(d_ff_40_q));  // open: Qn, preset, en, reset
  or or_5 (S[6], and_56_out, and_55_out, and_54_out, and_53_out, and_52_out, and_51_out, and_50_out, and_49_out);
  and and_49 (and_49_out, and_1_out, d_ff_33_q);
  and and_50 (and_50_out, and_2_out, d_ff_34_q);
  and and_51 (and_51_out, and_3_out, d_ff_35_q);
  and and_52 (and_52_out, and_4_out, d_ff_36_q);
  and and_53 (and_53_out, and_5_out, d_ff_37_q);
  and and_54 (and_54_out, and_6_out, d_ff_38_q);
  and and_55 (and_55_out, and_7_out, d_ff_39_q);
  and and_56 (and_56_out, and_8_out, d_ff_40_q);
  or or_6 (S[5], and_64_out, and_63_out, and_62_out, and_61_out, and_60_out, and_59_out, and_58_out, and_57_out);
  D_Flip_Flop d_ff_41 (.clk(and_9_out), .D(Input[5]), .Q(d_ff_41_q));  // open: Qn, preset, en, reset
  and and_57 (and_57_out, and_1_out, d_ff_41_q);
  D_Flip_Flop d_ff_42 (.clk(and_10_out), .D(Input[5]), .Q(d_ff_42_q));  // open: Qn, preset, en, reset
  and and_58 (and_58_out, and_2_out, d_ff_42_q);
  D_Flip_Flop d_ff_43 (.clk(and_11_out), .D(Input[5]), .Q(d_ff_43_q));  // open: Qn, preset, en, reset
  and and_59 (and_59_out, and_3_out, d_ff_43_q);
  D_Flip_Flop d_ff_44 (.clk(and_12_out), .D(Input[5]), .Q(d_ff_44_q));  // open: Qn, preset, en, reset
  and and_60 (and_60_out, and_4_out, d_ff_44_q);
  D_Flip_Flop d_ff_45 (.clk(and_13_out), .D(Input[5]), .Q(d_ff_45_q));  // open: Qn, preset, en, reset
  and and_61 (and_61_out, and_5_out, d_ff_45_q);
  D_Flip_Flop d_ff_46 (.clk(and_14_out), .D(Input[5]), .Q(d_ff_46_q));  // open: Qn, preset, en, reset
  and and_62 (and_62_out, and_6_out, d_ff_46_q);
  D_Flip_Flop d_ff_47 (.clk(and_15_out), .D(Input[5]), .Q(d_ff_47_q));  // open: Qn, preset, en, reset
  and and_63 (and_63_out, and_7_out, d_ff_47_q);
  D_Flip_Flop d_ff_48 (.clk(and_16_out), .D(Input[5]), .Q(d_ff_48_q));  // open: Qn, preset, en, reset
  and and_64 (and_64_out, and_8_out, d_ff_48_q);
  D_Flip_Flop d_ff_49 (.clk(and_9_out), .D(Input[4]), .Q(d_ff_49_q));  // open: Qn, preset, en, reset
  D_Flip_Flop d_ff_50 (.clk(and_10_out), .D(Input[4]), .Q(d_ff_50_q));  // open: Qn, preset, en, reset
  D_Flip_Flop d_ff_51 (.clk(and_11_out), .D(Input[4]), .Q(d_ff_51_q));  // open: Qn, preset, en, reset
  D_Flip_Flop d_ff_52 (.clk(and_12_out), .D(Input[4]), .Q(d_ff_52_q));  // open: Qn, preset, en, reset
  D_Flip_Flop d_ff_53 (.clk(and_13_out), .D(Input[4]), .Q(d_ff_53_q));  // open: Qn, preset, en, reset
  D_Flip_Flop d_ff_54 (.clk(and_14_out), .D(Input[4]), .Q(d_ff_54_q));  // open: Qn, preset, en, reset
  D_Flip_Flop d_ff_55 (.clk(and_15_out), .D(Input[4]), .Q(d_ff_55_q));  // open: Qn, preset, en, reset
  D_Flip_Flop d_ff_56 (.clk(and_16_out), .D(Input[4]), .Q(d_ff_56_q));  // open: Qn, preset, en, reset
  or or_7 (S[4], and_72_out, and_71_out, and_70_out, and_69_out, and_68_out, and_67_out, and_66_out, and_65_out);
  and and_65 (and_65_out, and_1_out, d_ff_49_q);
  and and_66 (and_66_out, and_2_out, d_ff_50_q);
  and and_67 (and_67_out, and_3_out, d_ff_51_q);
  and and_68 (and_68_out, and_4_out, d_ff_52_q);
  and and_69 (and_69_out, and_5_out, d_ff_53_q);
  and and_70 (and_70_out, and_6_out, d_ff_54_q);
  and and_71 (and_71_out, and_7_out, d_ff_55_q);
  and and_72 (and_72_out, and_8_out, d_ff_56_q);
  D_Flip_Flop d_ff_57 (.clk(and_9_out), .D(Input[3]), .Q(d_ff_57_q));  // open: Qn, preset, en, reset
  D_Flip_Flop d_ff_58 (.clk(and_10_out), .D(Input[3]), .Q(d_ff_58_q));  // open: Qn, preset, en, reset
  D_Flip_Flop d_ff_59 (.clk(and_11_out), .D(Input[3]), .Q(d_ff_59_q));  // open: Qn, preset, en, reset
  D_Flip_Flop d_ff_60 (.clk(and_12_out), .D(Input[3]), .Q(d_ff_60_q));  // open: Qn, preset, en, reset
  D_Flip_Flop d_ff_61 (.clk(and_13_out), .D(Input[3]), .Q(d_ff_61_q));  // open: Qn, preset, en, reset
  D_Flip_Flop d_ff_62 (.clk(and_14_out), .D(Input[3]), .Q(d_ff_62_q));  // open: Qn, preset, en, reset
  D_Flip_Flop d_ff_63 (.clk(and_15_out), .D(Input[3]), .Q(d_ff_63_q));  // open: Qn, preset, en, reset
  D_Flip_Flop d_ff_64 (.clk(and_16_out), .D(Input[3]), .Q(d_ff_64_q));  // open: Qn, preset, en, reset
  or or_8 (S[3], and_80_out, and_79_out, and_78_out, and_77_out, and_76_out, and_75_out, and_74_out, and_73_out);
  and and_73 (and_73_out, and_1_out, d_ff_57_q);
  and and_74 (and_74_out, and_2_out, d_ff_58_q);
  and and_75 (and_75_out, and_3_out, d_ff_59_q);
  and and_76 (and_76_out, and_4_out, d_ff_60_q);
  and and_77 (and_77_out, and_5_out, d_ff_61_q);
  and and_78 (and_78_out, and_6_out, d_ff_62_q);
  and and_79 (and_79_out, and_7_out, d_ff_63_q);
  and and_80 (and_80_out, and_8_out, d_ff_64_q);
  D_Flip_Flop d_ff_65 (.clk(and_9_out), .D(Input[2]), .Q(d_ff_65_q));  // open: Qn, preset, en, reset
  D_Flip_Flop d_ff_66 (.clk(and_10_out), .D(Input[2]), .Q(d_ff_66_q));  // open: Qn, preset, en, reset
  D_Flip_Flop d_ff_67 (.clk(and_11_out), .D(Input[2]), .Q(d_ff_67_q));  // open: Qn, preset, en, reset
  D_Flip_Flop d_ff_68 (.clk(and_12_out), .D(Input[2]), .Q(d_ff_68_q));  // open: Qn, preset, en, reset
  D_Flip_Flop d_ff_69 (.clk(and_13_out), .D(Input[2]), .Q(d_ff_69_q));  // open: Qn, preset, en, reset
  D_Flip_Flop d_ff_70 (.clk(and_14_out), .D(Input[2]), .Q(d_ff_70_q));  // open: Qn, preset, en, reset
  D_Flip_Flop d_ff_71 (.clk(and_15_out), .D(Input[2]), .Q(d_ff_71_q));  // open: Qn, preset, en, reset
  D_Flip_Flop d_ff_72 (.clk(and_16_out), .D(Input[2]), .Q(d_ff_72_q));  // open: Qn, preset, en, reset
  or or_9 (S[2], and_88_out, and_87_out, and_86_out, and_85_out, and_84_out, and_83_out, and_82_out, and_81_out);
  and and_81 (and_81_out, and_1_out, d_ff_65_q);
  and and_82 (and_82_out, and_2_out, d_ff_66_q);
  and and_83 (and_83_out, and_3_out, d_ff_67_q);
  and and_84 (and_84_out, and_4_out, d_ff_68_q);
  and and_85 (and_85_out, and_5_out, d_ff_69_q);
  and and_86 (and_86_out, and_6_out, d_ff_70_q);
  and and_87 (and_87_out, and_7_out, d_ff_71_q);
  and and_88 (and_88_out, and_8_out, d_ff_72_q);
  D_Flip_Flop d_ff_73 (.clk(and_9_out), .D(Input[1]), .Q(d_ff_73_q));  // open: Qn, preset, en, reset
  D_Flip_Flop d_ff_74 (.clk(and_10_out), .D(Input[1]), .Q(d_ff_74_q));  // open: Qn, preset, en, reset
  D_Flip_Flop d_ff_75 (.clk(and_11_out), .D(Input[1]), .Q(d_ff_75_q));  // open: Qn, preset, en, reset
  D_Flip_Flop d_ff_76 (.clk(and_12_out), .D(Input[1]), .Q(d_ff_76_q));  // open: Qn, preset, en, reset
  D_Flip_Flop d_ff_77 (.clk(and_13_out), .D(Input[1]), .Q(d_ff_77_q));  // open: Qn, preset, en, reset
  D_Flip_Flop d_ff_78 (.clk(and_14_out), .D(Input[1]), .Q(d_ff_78_q));  // open: Qn, preset, en, reset
  D_Flip_Flop d_ff_79 (.clk(and_15_out), .D(Input[1]), .Q(d_ff_79_q));  // open: Qn, preset, en, reset
  D_Flip_Flop d_ff_80 (.clk(and_16_out), .D(Input[1]), .Q(d_ff_80_q));  // open: Qn, preset, en, reset
  or or_10 (S[1], and_96_out, and_95_out, and_94_out, and_93_out, and_92_out, and_91_out, and_90_out, and_89_out);
  and and_89 (and_89_out, and_1_out, d_ff_73_q);
  and and_90 (and_90_out, and_2_out, d_ff_74_q);
  and and_91 (and_91_out, and_3_out, d_ff_75_q);
  and and_92 (and_92_out, and_4_out, d_ff_76_q);
  and and_93 (and_93_out, and_5_out, d_ff_77_q);
  and and_94 (and_94_out, and_6_out, d_ff_78_q);
  and and_95 (and_95_out, and_7_out, d_ff_79_q);
  and and_96 (and_96_out, and_8_out, d_ff_80_q);
  D_Flip_Flop d_ff_81 (.clk(and_9_out), .D(Input[0]), .Q(d_ff_81_q));  // open: Qn, preset, en, reset
  and and_97 (and_97_out, and_1_out, d_ff_81_q);
  D_Flip_Flop d_ff_82 (.clk(and_10_out), .D(Input[0]), .Q(d_ff_82_q));  // open: Qn, preset, en, reset
  and and_98 (and_98_out, and_2_out, d_ff_82_q);
  D_Flip_Flop d_ff_83 (.clk(and_11_out), .D(Input[0]), .Q(d_ff_83_q));  // open: Qn, preset, en, reset
  and and_99 (and_99_out, and_3_out, d_ff_83_q);
  D_Flip_Flop d_ff_84 (.clk(and_12_out), .D(Input[0]), .Q(d_ff_84_q));  // open: Qn, preset, en, reset
  and and_100 (and_100_out, and_4_out, d_ff_84_q);
  D_Flip_Flop d_ff_85 (.clk(and_13_out), .D(Input[0]), .Q(d_ff_85_q));  // open: Qn, preset, en, reset
  and and_101 (and_101_out, and_5_out, d_ff_85_q);
  D_Flip_Flop d_ff_86 (.clk(and_14_out), .D(Input[0]), .Q(d_ff_86_q));  // open: Qn, preset, en, reset
  and and_102 (and_102_out, and_6_out, d_ff_86_q);
  D_Flip_Flop d_ff_87 (.clk(and_15_out), .D(Input[0]), .Q(d_ff_87_q));  // open: Qn, preset, en, reset
  and and_103 (and_103_out, and_7_out, d_ff_87_q);
  D_Flip_Flop d_ff_88 (.clk(and_16_out), .D(Input[0]), .Q(d_ff_88_q));  // open: Qn, preset, en, reset
  and and_104 (and_104_out, and_8_out, d_ff_88_q);
  or or_11 (S[0], and_104_out, and_103_out, and_102_out, and_101_out, and_100_out, and_99_out, and_98_out, and_97_out);

  // Notes on the sheet:
  //   Artur Pigari Prata - 2101297
endmodule

module Contador (
  input  in_1,
  output [2:0] out_2
);

  T_Flip_Flop #(.trigger("falling")) t_ff_1 (.clk(in_1), .T(1'b1), .Q(out_2[0]));  // open: Qn, preset, reset, en
  T_Flip_Flop #(.trigger("falling")) t_ff_2 (.clk(out_2[0]), .T(1'b1), .Q(out_2[1]));  // open: Qn, preset, reset, en
  T_Flip_Flop #(.trigger("falling")) t_ff_3 (.clk(out_2[1]), .T(1'b1), .Q(out_2[2]));  // open: Qn, preset, reset, en

  // Notes on the sheet:
  //   Artur Pigari Prata - 2101297
endmodule

module Acumulador (
  input  [7:0] Input,
  input  R___W,
  output [7:0] Output
);

  D_Flip_Flop d_ff_1 (.clk(R___W), .D(Input[7]), .Q(Output[7]));  // open: Qn, preset, en, reset
  D_Flip_Flop d_ff_2 (.clk(R___W), .D(Input[6]), .Q(Output[6]));  // open: Qn, preset, en, reset
  D_Flip_Flop d_ff_3 (.clk(R___W), .D(Input[5]), .Q(Output[5]));  // open: Qn, preset, en, reset
  D_Flip_Flop d_ff_4 (.clk(R___W), .D(Input[4]), .Q(Output[4]));  // open: Qn, preset, en, reset
  D_Flip_Flop d_ff_5 (.clk(R___W), .D(Input[3]), .Q(Output[3]));  // open: Qn, preset, en, reset
  D_Flip_Flop d_ff_6 (.clk(R___W), .D(Input[2]), .Q(Output[2]));  // open: Qn, preset, en, reset
  D_Flip_Flop d_ff_7 (.clk(R___W), .D(Input[1]), .Q(Output[1]));  // open: Qn, preset, en, reset
  D_Flip_Flop d_ff_8 (.clk(R___W), .D(Input[0]), .Q(Output[0]));  // open: Qn, preset, en, reset

  // Notes on the sheet:
  //   Artur Pigari Prata - 2101297
endmodule

module somador_subtrator (
  input  [7:0] A,
  input  [7:0] B,
  input  in_3,
  output [7:0] S
);

  wire and_1_out, and_2_out, and_3_out, and_4_out, and_5_out, and_6_out, and_7_out, and_8_out, and_9_out,
       and_10_out, and_11_out, and_12_out, and_13_out, and_14_out, and_15_out, and_16_out, and_17_out,
       and_18_out, and_19_out, and_20_out, and_21_out, and_22_out, and_23_out, and_24_out, and_25_out,
       and_26_out, and_27_out, and_28_out, or_1_out, or_2_out, or_3_out, or_4_out, or_5_out, or_6_out,
       or_7_out;
  wire [7:0] G_out, P_out, xor_1_out;

  // Probe on A
  // Probe on S
  // Probe on B
  assign xor_1_out = B ^ {8{in_3}};  // XOR_Gate xor_1, 8 bits wide
  assign P_out = A | xor_1_out;  // OR_Gate P, 8 bits wide
  assign G_out = A & xor_1_out;  // AND_Gate G, 8 bits wide
  soma1b soma1b_1 (.A(A[7]), .B(xor_1_out[7]), .Cin(or_1_out), .S(S[7]));
  and and_1 (and_1_out, P_out[6], G_out[5]);
  and and_2 (and_2_out, P_out[6], P_out[5], G_out[4]);
  or or_1 (or_1_out, G_out[6], and_1_out, and_2_out, and_3_out, and_4_out, and_5_out, and_6_out, and_7_out);
  and and_3 (and_3_out, P_out[6], P_out[5], P_out[4], G_out[3]);
  and and_4 (and_4_out, P_out[6], P_out[5], P_out[4], P_out[3], G_out[2]);
  and and_5 (and_5_out, P_out[6], P_out[5], P_out[4], P_out[3], P_out[2], G_out[1]);
  and and_6 (and_6_out, P_out[6], P_out[5], P_out[4], P_out[3], P_out[2], P_out[1], G_out[0]);
  and and_7 (and_7_out, P_out[6], P_out[5], P_out[4], P_out[3], P_out[2], P_out[1], P_out[0], in_3);
  soma1b soma1b_2 (.A(A[6]), .B(xor_1_out[6]), .Cin(or_2_out), .S(S[6]));
  and and_8 (and_8_out, P_out[5], P_out[4], G_out[3]);
  and and_9 (and_9_out, P_out[5], G_out[4]);
  or or_2 (or_2_out, G_out[5], and_9_out, and_8_out, and_10_out, and_12_out, and_11_out, and_13_out);
  and and_10 (and_10_out, P_out[5], P_out[4], P_out[3], G_out[2]);
  and and_11 (and_11_out, P_out[5], P_out[4], P_out[3], P_out[2], P_out[1], G_out[0]);
  and and_12 (and_12_out, P_out[5], P_out[4], P_out[3], P_out[2], G_out[1]);
  and and_13 (and_13_out, P_out[5], P_out[4], P_out[3], P_out[2], P_out[1], P_out[0], in_3);
  soma1b soma1b_3 (.A(A[5]), .B(xor_1_out[5]), .Cin(or_3_out), .S(S[5]));
  and and_14 (and_14_out, P_out[4], P_out[3]);
  and and_15 (and_15_out, P_out[4], P_out[3], G_out[2]);
  or or_3 (or_3_out, G_out[4], and_14_out, and_15_out, and_16_out, and_17_out, and_18_out);
  and and_16 (and_16_out, P_out[4], P_out[3], P_out[2], G_out[1]);
  and and_17 (and_17_out, P_out[4], P_out[3], P_out[2], P_out[1], G_out[0]);
  and and_18 (and_18_out, P_out[4], P_out[3], P_out[2], P_out[1], P_out[0], in_3);
  soma1b soma1b_4 (.A(A[4]), .B(xor_1_out[4]), .Cin(or_4_out), .S(S[4]));
  and and_19 (and_19_out, P_out[3], P_out[2], G_out[1]);
  and and_20 (and_20_out, P_out[3], G_out[2]);
  or or_4 (or_4_out, G_out[3], and_20_out, and_19_out, and_21_out, and_22_out);
  and and_21 (and_21_out, P_out[3], P_out[2], P_out[1], G_out[0]);
  and and_22 (and_22_out, P_out[3], P_out[2], P_out[1], P_out[0], in_3);
  soma1b soma1b_5 (.A(A[3]), .B(xor_1_out[3]), .Cin(or_5_out), .S(S[3]));
  and and_23 (and_23_out, P_out[2], G_out[1]);
  and and_24 (and_24_out, P_out[2], P_out[1], G_out[0]);
  or or_5 (or_5_out, G_out[2], and_23_out, and_24_out, and_25_out);
  and and_25 (and_25_out, P_out[2], P_out[1], P_out[0], in_3);
  and and_26 (and_26_out, P_out[1], G_out[0]);
  or or_6 (or_6_out, G_out[1], and_26_out, and_27_out);
  soma1b soma1b_6 (.A(A[2]), .B(xor_1_out[2]), .Cin(or_6_out), .S(S[2]));
  and and_27 (and_27_out, P_out[0], P_out[1], in_3);
  or or_7 (or_7_out, G_out[0], and_28_out);
  soma1b soma1b_7 (.A(A[1]), .B(xor_1_out[1]), .Cin(or_7_out), .S(S[1]));
  and and_28 (and_28_out, P_out[0], in_3);
  soma1b soma1b_8 (.A(A[0]), .B(xor_1_out[0]), .Cin(in_3), .S(S[0]));

  // Notes on the sheet:
  //   Artur Pigari Prata - 2101297
endmodule

module soma1b (
  input  A,
  input  B,
  input  Cin,
  output S
);

  wire xor_1_out;

  xor xor_1 (xor_1_out, B, Cin);
  xor xor_2 (S, xor_1_out, A);

  // Notes on the sheet:
  //   Artur Pigari Prata - 2101297
endmodule

module output8 (
  input  in_1,
  output [7:0] out_2
);


  assign out_2 = {8{in_1}};

  // Notes on the sheet:
  //   Artur Pigari Prata - 2101297
endmodule
